# Fritzing sketch WiringDiagram (saved by Fritzing 0.9.5d)
stripboards: 1

parts:
  M2 = Stepper Motor - Bipolar
  Pololu_A1 = Pololu A4988 [package=SO16]
  M3 = Stepper Motor - Bipolar
  Pololu_A2 = Pololu A4988 [package=SO16]
  C2 = Electrolytic Capacitor [capacitance=10μF package="0605 [SMD, electrolytic]"]
  M4 = Stepper Motor - Bipolar
  Pololu_A3 = Pololu A4988 [package=SO16]
  C3 = Electrolytic Capacitor [capacitance=10μF package="0605 [SMD, electrolytic]"]
  M5 = Stepper Motor - Bipolar
  Pololu_A4 = Pololu A4988 [package=SO16]
  C4 = Electrolytic Capacitor [capacitance=10μF package="0605 [SMD, electrolytic]"]
  C1 = Electrolytic Capacitor [capacitance=10μF package="0605 [SMD, electrolytic]"]
  HC-SR04_Sensor_1 = HC-SR04 Ultrasonic Distance Sensor
  Mod1 = ESP32 - CAM
  Mod2 = ESP32 - CAM
  M6 = RioRand LM2596
  J1 = Basic Servo
  J2 = Basic Servo
  BMS1 = BMS
  ESP1 = DIP - 42 pins
  LiPo1 = DIP - 6 pins [package=Battery]

nets:
  N1: M2.A, Pololu_A1.2B
  N2: M2.C, Pololu_A1.2A
  N3: M2.B, Pololu_A1.1A
  N4: M2.D, Pololu_A1.1B
  N5: Pololu_A1.RESET, Pololu_A1.SLEEP
  N6: Pololu_A1.STEP, ESP1.GPIO02
  GND: Pololu_A1.GND#8, Pololu_A2.GND#8, Pololu_A3.GND#8, Pololu_A4.GND#8, HC-SR04_Sensor_1.GND, Mod1.GND, Mod2.GND, M6.Pin_4, J1.gnd, J2.gnd, ESP1.GND
  VDD: Pololu_A1.VDD, Pololu_A2.VDD, Pololu_A3.VDD, Pololu_A4.VDD, HC-SR04_Sensor_1.VCC, Mod1.5V, Mod2.5V, M6.Pin_3, J1.vcc, J2.vcc, ESP1.5v0
  N7: Pololu_A1.GND#14, Pololu_A2.GND#14, C2.-, Pololu_A3.GND#14, C3.-, Pololu_A4.GND#14, C4.-, C1.-, M6.Pin_2, BMS1.Load_-
  N8: Pololu_A1.VMOT, Pololu_A2.VMOT, C2.+, Pololu_A3.VMOT, C3.+, Pololu_A4.VMOT, C4.+, C1.+, M6.Pin_1, BMS1.Load_+
  N9: M3.A, Pololu_A2.2B
  N10: M3.C, Pololu_A2.2A
  N11: M3.B, Pololu_A2.1A
  N12: M3.D, Pololu_A2.1B
  N13: Pololu_A2.RESET, Pololu_A2.SLEEP
  N14: Pololu_A2.STEP, ESP1.GPIO04
  N15: Pololu_A2.DIR, ESP1.GPIO03
  N16: M4.A, Pololu_A3.2B
  N17: M4.C, Pololu_A3.2A
  N18: M4.B, Pololu_A3.1A
  N19: M4.D, Pololu_A3.1B
  N20: Pololu_A3.RESET, Pololu_A3.SLEEP
  N21: Pololu_A3.STEP, ESP1.GPIO06
  N22: Pololu_A3.DIR, ESP1.GPIO05
  N23: M5.A, Pololu_A4.2B
  N24: M5.C, Pololu_A4.2A
  N25: M5.B, Pololu_A4.1A
  N26: M5.D, Pololu_A4.1B
  N27: Pololu_A4.RESET, Pololu_A4.SLEEP
  N28: Pololu_A4.STEP, ESP1.GPIO08
  N29: Pololu_A4.DIR, ESP1.GPIO07
  N30: HC-SR04_Sensor_1.TRIG, ESP1.GPIO13
  N31: HC-SR04_Sensor_1.ECHO, ESP1.GPIO12
  N32: J1.pulse, ESP1.GPIO37
  N33: J2.pulse, ESP1.GPIO38
  N34: BMS1.0V, LiPo1.V-, LiPo1.0V
  N35: BMS1.4.2V, LiPo1.4.2V
  N36: BMS1.8.4V, LiPo1.8.4V
  N37: BMS1.12.6V, LiPo1.V+, LiPo1.12.6V

custom parts:
  ESP32 - CAM: The ESP32-CAM has a very competitive small-size camera module that can operate independently as a minimum system with a footprint of only 27*40.5*4.5mm and a deep sleep current of up to 6mA.
  BMS: BMS for 3S battery
  DIP - 42 pins: ESP32-S2-DevKitM-1
  DIP - 6 pins: A LiPo 3S
